# Fritzing sketch NodeMcuCar (saved by Fritzing 0.9.3b)

parts:
  NodeMCU = NodeMCU V1.0
  右电机 = DC Motor
  左电机 = DC Motor
  L298N = H-Bridge with L298N
  VCC1 = Battery

nets:
  N1: NodeMCU.D1, L298N.ENA
  N2: NodeMCU.D2, L298N.IN1
  N3: NodeMCU.D3, L298N.IN2
  N4: NodeMCU.D4, L298N.IN3
  3V3: NodeMCU.3V3, L298N.5V
  GND: NodeMCU.GND, L298N.GND, VCC1.-
  N5: NodeMCU.D5, L298N.IN4
  N6: NodeMCU.D6, L298N.ENB
  VIN: NodeMCU.Vin, L298N.12V, VCC1.+
  N7: 右电机.pin_1, L298N.M2-02
  N8: 右电机.pin_2, L298N.M2-01
  N9: 左电机.pin_1, L298N.M1-02
  N10: 左电机.pin_2, L298N.M1-01

custom parts:
  NodeMCU V1.0: ESP8266 based NodeMCU
  H-Bridge with L298N: h-bridge
